# Fritzing sketch ReactionGameV1 (saved by Fritzing 0.9.3b)
breadboards: 1

parts:
  Part1 = Arduino Uno (Rev3)
  S1 = Pushbutton [package="[THT]"]
  S2 = Pushbutton [package="[THT]"]
  LED1 = LED - 5mm [color="Green (555nm)" package="5 mm [THT]"]
  LED2 = LED - 5mm [color="Yellow (595nm)" package="5 mm [THT]"]
  LED3 = LED - 5mm [color="Red (633nm)" package="5 mm [THT]"]
  LED4 = LED - 5mm [color="Red (633nm)" package="5 mm [THT]"]
  LED5 = LED - 5mm [color="Yellow (595nm)" package="5 mm [THT]"]
  R1 = Resistor [tolerance=±5% resistance=220 package=THT]
  R2 = Resistor [tolerance=±5% resistance=220 package=THT]
  R3 = Resistor [tolerance=±5% resistance=220 package=THT]
  R4 = Resistor [tolerance=±5% resistance=220 package=THT]

nets:
  N1: Part1.D9_PWM, LED1.cathode
  N2: Part1.D10_PWM/SS, LED2.cathode
  N3: Part1.D11_PWM/MOSI, LED3.cathode
  N4: Part1.D13/SCK, S1.Pin_3, S1.Pin_4, R3.Pin_0
  N5: Part1.D4, S2.Pin_1, S2.Pin_2, R4.Pin_0
  N6: Part1.D5_PWM, LED4.cathode
  N7: Part1.D6_PWM, LED5.cathode
  N8: Part1.5V, R1.Pin_1, R2.Pin_1
  N9: Part1.GND, R3.Pin_1, R4.Pin_1
  N10: S1.Pin_1, S1.Pin_2, R1.Pin_0
  N11: S2.Pin_3, S2.Pin_4, R2.Pin_0
