# Fritzing sketch ReactionGameV3 (saved by Fritzing 0.9.3b)
breadboards: 2

parts:
  Part2 = Arduino Uno (Rev3)
  S4 = Pushbutton [package="[THT]"]
  S5 = Pushbutton [package="[THT]"]
  R14 = Resistor [tolerance=±5% resistance=10k package=THT]
  R15 = Resistor [tolerance=±5% resistance=10k package=THT]
  R16 = Resistor [tolerance=±5% resistance=220 package=THT]
  R17 = Resistor [tolerance=±5% resistance=220 package=THT]
  LED8 = LED - 5mm [color="Red (633nm)" package="5 mm [THT]"]
  LED9 = LED - 5mm [color="Red (633nm)" package="5 mm [THT]"]
  LED10 = LED - 5mm [color="Green (555nm)" package="5 mm [THT]"]
  R18 = Resistor [tolerance=±5% resistance=1k package=THT]
  R19 = Resistor [tolerance=±5% resistance=1k package=THT]
  R20 = Resistor [tolerance=±5% resistance=1k package=THT]

nets:
  N1: Part2.D8, S4.Pin_3, S4.Pin_4, R15.Pin_0
  N2: Part2.D9_PWM, LED9.cathode
  N3: Part2.D10_PWM/SS, LED10.cathode
  N4: Part2.D11_PWM/MOSI, LED8.cathode
  N5: Part2.D12/MISO, S5.Pin_1, S5.Pin_2, R16.Pin_0
  N6: Part2.5V, R16.Pin_1, R17.Pin_1, R18.Pin_1, R19.Pin_1, R20.Pin_1
  N7: Part2.GND, R14.Pin_1, R15.Pin_1
  N8: S4.Pin_1, S4.Pin_2, R17.Pin_0
  N9: S5.Pin_3, S5.Pin_4, R14.Pin_0
  N10: LED8.anode, R20.Pin_0
  N11: LED9.anode, R19.Pin_0
  N12: LED10.anode, R18.Pin_0
